# Fritzing sketch nail2nail (saved by Fritzing 0.9.0b)
breadboards: 1

parts:
  Part1 = Arduino Uno (Rev3)
  R1 = Resistor [tolerance=±5% resistance=220 package=THT]
  ANT1 = Antenna  # not connected
  ANT2 = Antenna
  U1 = Optocoupler [package=THT]

nets:
  N1: Part1.A0, R1.Pin_0
  N2: Part1.A4/SDA, U1.Pin_2
  N3: Part1.A5/SCL, U1.Pin_1
  N4: Part1.D2, R1.Pin_1
  N5: Part1.D3_PWM, ANT2.antenna_lead

custom parts:
  Optocoupler: Optocoupler - keeps you from frying your stuff!
